# Fritzing sketch Schematic_Circut (saved by Fritzing 0.9.4)
breadboards: 1

parts:
  Part1 = Arduino Uno (Rev3)
  R1 = Resistor [tolerance=±5% resistance=150 package=THT]
  LED2 = LED - 5mm [color="Green (555nm)" package="5 mm [THT]"]
  R2 = Resistor [tolerance=±5% resistance=150 package=THT]
  LED3 = LED - 5mm [color="Green (555nm)" package="5 mm [THT]"]
  R3 = Resistor [tolerance=±5% resistance=150 package=THT]
  LED1 = LED - 5mm [color="Green (555nm)" package="5 mm [THT]"]

nets (from the schematic view):
  N1: Part1.D11_PWM/MOSI, R3.Pin_1
  N2: Part1.D12/MISO, R2.Pin_0
  N3: Part1.D13/SCK, R1.Pin_1
  N4: Part1.GND, LED2.anode, LED3.anode, LED1.anode
  N5: R1.Pin_0, LED1.cathode
  N6: LED2.cathode, R2.Pin_1
  N7: LED3.cathode, R3.Pin_0
